# Fritzing sketch Develop Station (saved by Fritzing 0.9.3b)
perfboards: 2

parts:
  Part1 = Analog Digital MUX Breakout
  R1 = Resistor [tolerance=±5% resistance=220 package=THT]  # not connected
  R2 = Resistor [tolerance=±5% resistance=220 package=THT]  # not connected
  R3 = Resistor [tolerance=±5% resistance=220 package=THT]  # not connected
  R4 = Resistor [tolerance=±5% resistance=220 package=THT]  # not connected
  R5 = Resistor [tolerance=±5% resistance=220 package=THT]  # not connected
  R6 = Resistor [tolerance=±5% resistance=220 package=THT]
  LED1 = LED - 5mm [color="Red (633nm)" package="5 mm [THT]"]
  S1 = Pushbutton [package="[THT]"]
  Q1 = NPN-Transistor [package="TO92 [THT]"]
  R8 = Resistor [tolerance=±5% resistance=220 package=THT]
  SW1 = DIP Switch 8 Position [package=dipswitch-08]
  R7 = Resistor [tolerance=±5% resistance=220 package=THT]
  R9 = Rotary Potentiometer (Small) [maximum_resistance=100kΩ package=THT]
  Pro_Micro1 = Pro Micro  # not connected
  R10 = Resistor [tolerance=±5% resistance=220 package="0805 [SMD]"]  # not connected

nets:
  N1: Part1.GND, SW1.1, R9.wiper
  N2: Part1.VCC, R6.Pin_0, R7.Pin_0
  N3: R6.Pin_1, LED1.anode
  N4: LED1.cathode, Q1.C
  N5: S1.Pin_1, S1.Pin_2
  N6: S1.Pin_3, S1.Pin_4
  N7: Q1.E, SW1.8
  N8: Q1.B, R8.Pin_0

custom parts:
  Pro Micro: The SparkFun Pro Micro is a complete USB-based microcontoller development system, in a very small footprint, capable of implementing many types of projects. All programming can be done via the USB port.
